// Logisim project Quartz_version_0.circ as structural Verilog: 1 circuit, main circuit main
module main (
);

  wire and_1_out, and_2_out, C_CLOCK, C_MAR_LATCH, C_MEM_READ, C_MEM_WRITE, C_PC_ENABLE, C_PC_LATCH, C_RESET,
       not_1_out, not_2_out;
  wire [7:0] controlled_buffer_2_out, controlled_buffer_4_out, MDR_q, ram_1_dout, rom_1_data;
  wire [7:7] pull_resistor_1_node;
  wire [15:0] controlled_buffer_1_out, MAR_q, PC_q;

  // Probe on C_CLOCK
  // Probe on C_PC_LATCH
  // Probe on C_PC_ENABLE
  // Probe on C_MAR_LATCH
  // Probe on C_MEM_WRITE
  // Probe on C_RESET
  // Probe on C_MEM_READ
  // Probe on pull_resistor_1_node[7]
  Pull_Resistor pull_resistor_1 (.node({pull_resistor_1_node[7], C_MEM_READ, C_RESET, C_MEM_WRITE, C_MAR_LATCH, C_PC_ENABLE, C_PC_LATCH, C_CLOCK}));
  // Switch switch_1: pin names not known; wires that end beside it: C_CLOCK
  // Switch switch_2: pin names not known; wires that end beside it: C_PC_LATCH
  // Switch switch_3: pin names not known; wires that end beside it: C_PC_ENABLE
  // Switch switch_4: pin names not known; wires that end beside it: C_MAR_LATCH
  // Switch switch_5: pin names not known; wires that end beside it: C_MEM_WRITE
  // Switch switch_6: pin names not known; wires that end beside it: C_RESET
  // Switch switch_7: pin names not known; wires that end beside it: C_MEM_READ
  // Switch switch_8: pin names not known; wires that end beside it: pull_resistor_1_node[7], 1'b1
  Register #(.width(16)) PC (.D(controlled_buffer_1_out), .en(C_PC_LATCH), .clk(C_CLOCK), .Q(PC_q), .clr(C_RESET));
  assign controlled_buffer_1_out = C_PC_ENABLE ? PC_q : 16'bz;  // Controlled_Buffer controlled_buffer_1
  Pull_Resistor pull_resistor_2 ();  // open: node
  // Probe on controlled_buffer_1_out
  Register #(.width(16)) MAR (.D(controlled_buffer_1_out), .en(C_MAR_LATCH), .clk(C_CLOCK), .Q(MAR_q), .clr(C_RESET));
  ROM #(.addrWidth(15)) rom_1 (.addr(MAR_q[14:0]), .data(rom_1_data));
  RAM #(.addrWidth(15)) ram_1 (
    .addr(MAR_q[14:0]), .we(C_MEM_WRITE), .oe(not_1_out), .clk(C_CLOCK), .din(controlled_buffer_4_out),
    .dout(ram_1_dout));
  not not_1 (not_1_out, C_MEM_WRITE);
  not not_2 (not_2_out, MAR_q[15]);
  and and_1 (and_1_out, C_MEM_READ, not_2_out);
  and and_2 (and_2_out, MAR_q[15], C_MEM_READ);
  assign controlled_buffer_2_out = and_1_out ? rom_1_data : 8'bz;  // Controlled_Buffer controlled_buffer_2
  assign controlled_buffer_2_out = and_2_out ? ram_1_dout : 8'bz;  // Controlled_Buffer controlled_buffer_3
  assign controlled_buffer_4_out = C_MEM_WRITE ? MDR_q : 8'bz;  // Controlled_Buffer controlled_buffer_4
  Register MDR (.D(controlled_buffer_2_out), .en(C_MEM_READ), .clk(C_CLOCK), .Q(MDR_q), .clr(C_RESET));
  // also tied to VCC on the sheet: {controlled_buffer_1_out[0], controlled_buffer_1_out[1], controlled_buffer_1_out[2], controlled_buffer_1_out[3], controlled_buffer_1_out[4], controlled_buffer_1_out[5], controlled_buffer_1_out[6], controlled_buffer_1_out[7], controlled_buffer_1_out[8], controlled_buffer_1_out[9], controlled_buffer_1_out[10], controlled_buffer_1_out[11], controlled_buffer_1_out[12], controlled_buffer_1_out[13], controlled_buffer_1_out[14], controlled_buffer_1_out[15]}

  // Notes on the sheet:
  //   contents of rom_1 (hex, n*v repeats v):
  //   de ad
endmodule
